# Fritzing sketch Illuminar Borad (saved by Fritzing 0.9.3b)
breadboards: 1

parts:
  Part1 = Arduino Uno (Rev3)
  Q2 = Basic FET N-Channel [package="TO220 [THT]"]
  R1 = Resistor [tolerance=±5% resistance=300 package=THT]
  LED1 = LED - 5mm [color="Orange (620nm)" package="5 mm [THT]"]
  R2 = PHOTOCELL [package=photocell]
  LED2 = LED - 5mm [color="Infrared (940nm)" package="5 mm [THT]"]
  Power_RGB1 = Prolight RGB 3 Watt Star  # not connected
  BAT1 = Battery Holders [package=battery-aa-kit]

nets:
  N1: Part1.A0, R2.P$1
  N2: Part1.D8, LED2.anode
  N3: Part1.D9_PWM, Q2.gate, R1.Pin_0
  N4: Part1.GND, Q2.source, R1.Pin_1, LED2.cathode, BAT1.-
  N5: Q2.drain, LED1.cathode
  N6: LED1.anode, BAT1.+
